// Logisim project Computadora bonita.circ as structural Verilog: 1 circuit, main circuit main
module main (
  input  Sumar,
  input  Bit,
  input  Bit_2,
  input  Bit_3,
  input  Bit_4,
  input  Escribir,
  input  Direccion_de_memoria,
  input  in_8,
  output out_9,
  output out_10,
  output out_11,
  output out_12,
  output out_13,
  output out_14,
  output out_15,
  output out_16,
  output out_17,
  output out_18,
  output out_19,
  output out_20,
  output out_21,
  output out_22,
  output out_23,
  output out_24,
  output out_25,
  output out_26,
  output out_27,
  output out_28,
  output out_29
);

  wire and_1_out, and_2_out, and_3_out, and_4_out, and_5_out, and_6_out, and_7_out, and_8_out, and_9_out,
       and_10_out, and_11_out, clock_1_out, multiplexer_1_out, multiplexer_2_out, multiplexer_3_out,
       multiplexer_4_out, multiplexer_5_out, multiplexer_6_out, multiplexer_7_out, multiplexer_8_out,
       multiplexer_9_out, multiplexer_10_out, multiplexer_11_out, multiplexer_12_out, multiplexer_13_out,
       multiplexer_14_out, multiplexer_15_out, multiplexer_16_out, multiplexer_17_out, multiplexer_18_out,
       multiplexer_19_out, multiplexer_20_out, not_1_out, not_2_out, not_3_out, not_4_out, or_1_out,
       or_2_out, or_3_out, xor_2_out, xor_4_out, xor_6_out;

  Multiplexer #(.enable("false")) multiplexer_1 (.in0(Bit_4), .in1(out_29), .out(multiplexer_1_out), .sel(Sumar));
  Multiplexer #(.enable("false")) multiplexer_2 (.in0(Bit_3), .in1(out_28), .out(multiplexer_2_out), .sel(Sumar));
  Multiplexer #(.enable("false")) multiplexer_3 (.in0(Bit_2), .in1(out_27), .out(multiplexer_3_out), .sel(Sumar));
  Multiplexer #(.enable("false")) multiplexer_4 (.in0(Bit), .in1(out_26), .out(multiplexer_4_out), .sel(Sumar));
  and and_1 (and_1_out, Direccion_de_memoria, in_8, or_1_out);
  Multiplexer #(.enable("false")) multiplexer_5 (
    .in0(out_9), .in1(multiplexer_1_out), .out(multiplexer_5_out), .sel(and_1_out));
  Multiplexer #(.enable("false")) multiplexer_6 (
    .in0(out_13), .in1(multiplexer_2_out), .out(multiplexer_6_out), .sel(and_1_out));
  Multiplexer #(.enable("false")) multiplexer_7 (
    .in0(out_17), .in1(multiplexer_3_out), .out(multiplexer_7_out), .sel(and_1_out));
  Multiplexer #(.enable("false")) multiplexer_8 (
    .in0(out_21), .in1(multiplexer_4_out), .out(multiplexer_8_out), .sel(and_1_out));
  Clock clock_1 (.out(clock_1_out));
  D_Flip_Flop #(.trigger("falling")) d_ff_1 (
    .clk(clock_1_out), .D(multiplexer_5_out), .Q(out_9));  // open: Qn, preset, en, reset
  D_Flip_Flop #(.trigger("falling")) d_ff_2 (
    .clk(clock_1_out), .D(multiplexer_6_out), .Q(out_13));  // open: Qn, preset, en, reset
  D_Flip_Flop #(.trigger("falling")) d_ff_3 (
    .clk(clock_1_out), .D(multiplexer_7_out), .Q(out_17));  // open: Qn, preset, en, reset
  D_Flip_Flop #(.trigger("falling")) d_ff_4 (
    .clk(clock_1_out), .D(multiplexer_8_out), .Q(out_21));  // open: Qn, preset, en, reset
  or or_1 (or_1_out, Sumar, Escribir);
  not not_1 (not_1_out, in_8);
  and and_2 (and_2_out, Direccion_de_memoria, not_1_out, or_1_out);
  Multiplexer #(.enable("false")) multiplexer_9 (
    .in0(out_10), .in1(multiplexer_1_out), .out(multiplexer_9_out), .sel(and_2_out));
  Multiplexer #(.enable("false")) multiplexer_10 (
    .in0(out_14), .in1(multiplexer_2_out), .out(multiplexer_10_out), .sel(and_2_out));
  Multiplexer #(.enable("false")) multiplexer_11 (
    .in0(out_18), .in1(multiplexer_3_out), .out(multiplexer_11_out), .sel(and_2_out));
  Multiplexer #(.enable("false")) multiplexer_12 (
    .in0(out_22), .in1(multiplexer_4_out), .out(multiplexer_12_out), .sel(and_2_out));
  D_Flip_Flop #(.trigger("falling")) d_ff_5 (
    .clk(clock_1_out), .D(multiplexer_9_out), .Q(out_10));  // open: Qn, preset, en, reset
  D_Flip_Flop #(.trigger("falling")) d_ff_6 (
    .clk(clock_1_out), .D(multiplexer_10_out), .Q(out_14));  // open: Qn, preset, en, reset
  D_Flip_Flop #(.trigger("falling")) d_ff_7 (
    .clk(clock_1_out), .D(multiplexer_11_out), .Q(out_18));  // open: Qn, preset, en, reset
  D_Flip_Flop #(.trigger("falling")) d_ff_8 (
    .clk(clock_1_out), .D(multiplexer_12_out), .Q(out_22));  // open: Qn, preset, en, reset
  xor xor_1 (out_29, out_11, out_12);
  not not_2 (not_2_out, Direccion_de_memoria);
  and and_3 (and_3_out, not_2_out, in_8, or_1_out);
  Multiplexer #(.enable("false")) multiplexer_13 (
    .in0(out_11), .in1(multiplexer_1_out), .out(multiplexer_13_out), .sel(and_3_out));
  Multiplexer #(.enable("false")) multiplexer_14 (
    .in0(out_15), .in1(multiplexer_2_out), .out(multiplexer_14_out), .sel(and_3_out));
  Multiplexer #(.enable("false")) multiplexer_15 (
    .in0(out_19), .in1(multiplexer_3_out), .out(multiplexer_15_out), .sel(and_3_out));
  Multiplexer #(.enable("false")) multiplexer_16 (
    .in0(out_23), .in1(multiplexer_4_out), .out(multiplexer_16_out), .sel(and_3_out));
  and and_4 (and_4_out, out_11, out_12);
  xor xor_2 (xor_2_out, and_4_out, out_15);
  and and_5 (and_5_out, xor_2_out, out_16);
  D_Flip_Flop #(.trigger("falling")) d_ff_9 (
    .clk(clock_1_out), .D(multiplexer_13_out), .Q(out_11));  // open: Qn, preset, en, reset
  D_Flip_Flop #(.trigger("falling")) d_ff_10 (
    .clk(clock_1_out), .D(multiplexer_14_out), .Q(out_15));  // open: Qn, preset, en, reset
  D_Flip_Flop #(.trigger("falling")) d_ff_11 (
    .clk(clock_1_out), .D(multiplexer_15_out), .Q(out_19));  // open: Qn, preset, en, reset
  D_Flip_Flop #(.trigger("falling")) d_ff_12 (
    .clk(clock_1_out), .D(multiplexer_16_out), .Q(out_23));  // open: Qn, preset, en, reset
  and and_6 (and_6_out, and_4_out, out_15);
  xor xor_3 (out_28, xor_2_out, out_16);
  or or_2 (or_2_out, and_6_out, and_5_out);
  not not_3 (not_3_out, in_8);
  not not_4 (not_4_out, Direccion_de_memoria);
  and and_7 (and_7_out, not_4_out, not_3_out, or_1_out);
  Multiplexer #(.enable("false")) multiplexer_17 (
    .in0(out_12), .in1(multiplexer_1_out), .out(multiplexer_17_out), .sel(and_7_out));
  Multiplexer #(.enable("false")) multiplexer_18 (
    .in0(out_16), .in1(multiplexer_2_out), .out(multiplexer_18_out), .sel(and_7_out));
  Multiplexer #(.enable("false")) multiplexer_19 (
    .in0(out_20), .in1(multiplexer_3_out), .out(multiplexer_19_out), .sel(and_7_out));
  Multiplexer #(.enable("false")) multiplexer_20 (
    .in0(out_24), .in1(multiplexer_4_out), .out(multiplexer_20_out), .sel(and_7_out));
  xor xor_4 (xor_4_out, out_19, or_2_out);
  and and_8 (and_8_out, xor_4_out, out_20);
  D_Flip_Flop #(.trigger("falling")) d_ff_13 (
    .clk(clock_1_out), .D(multiplexer_17_out), .Q(out_12));  // open: Qn, preset, en, reset
  D_Flip_Flop #(.trigger("falling")) d_ff_14 (
    .clk(clock_1_out), .D(multiplexer_18_out), .Q(out_16));  // open: Qn, preset, en, reset
  D_Flip_Flop #(.trigger("falling")) d_ff_15 (
    .clk(clock_1_out), .D(multiplexer_19_out), .Q(out_20));  // open: Qn, preset, en, reset
  D_Flip_Flop #(.trigger("falling")) d_ff_16 (
    .clk(clock_1_out), .D(multiplexer_20_out), .Q(out_24));  // open: Qn, preset, en, reset
  and and_9 (and_9_out, out_19, or_2_out);
  xor xor_5 (out_27, xor_4_out, out_20);
  or or_3 (or_3_out, and_9_out, and_8_out);
  xor xor_6 (xor_6_out, or_3_out, out_23);
  buf and_10 (and_10_out, out_24);  // AND_Gate
  and and_11 (and_11_out, or_3_out, out_23);
  xor xor_7 (out_26, xor_6_out, out_24);
  or or_4 (out_25, and_11_out, and_10_out);
endmodule
