// Logisim project RAM - 4bits.circ as structural Verilog: 1 circuit, main circuit main
module main (
  input  Direccion_de_memoria,
  input  Bit,
  input  Bit_2,
  input  Bit_3,
  input  Bit_4,
  output out_6,
  output out_7,
  output out_8,
  output out_9,
  output out_10,
  output out_11,
  output out_12,
  output out_13
);

  wire clock_1_out, demultiplexer_1_out0, demultiplexer_1_out1, demultiplexer_2_out0, demultiplexer_2_out1,
       demultiplexer_3_out0, demultiplexer_3_out1, demultiplexer_4_out0, demultiplexer_4_out1,
       multiplexer_1_out, multiplexer_2_out, multiplexer_3_out, multiplexer_4_out, multiplexer_5_out,
       multiplexer_6_out, multiplexer_7_out, multiplexer_8_out, not_1_out, not_2_out;

  Demultiplexer #(.enable("false")) demultiplexer_1 (
    .out0(demultiplexer_1_out0), .out1(demultiplexer_1_out1), .in(Bit), .sel(Direccion_de_memoria));
  Demultiplexer #(.enable("false")) demultiplexer_2 (
    .out0(demultiplexer_2_out0), .out1(demultiplexer_2_out1), .in(Bit_2), .sel(Direccion_de_memoria));
  Demultiplexer #(.enable("false")) demultiplexer_3 (
    .out0(demultiplexer_3_out0), .out1(demultiplexer_3_out1), .in(Bit_3), .sel(Direccion_de_memoria));
  Demultiplexer #(.enable("false")) demultiplexer_4 (
    .out0(demultiplexer_4_out0), .out1(demultiplexer_4_out1), .in(Bit_4), .sel(Direccion_de_memoria));
  not not_1 (not_1_out, Direccion_de_memoria);
  Multiplexer #(.enable("false")) multiplexer_1 (
    .in0(out_6), .in1(demultiplexer_1_out0), .out(multiplexer_1_out), .sel(not_1_out));
  Multiplexer #(.enable("false")) multiplexer_2 (
    .in0(out_8), .in1(demultiplexer_2_out0), .out(multiplexer_2_out), .sel(not_1_out));
  Multiplexer #(.enable("false")) multiplexer_3 (
    .in0(out_10), .in1(demultiplexer_3_out0), .out(multiplexer_3_out), .sel(not_1_out));
  Multiplexer #(.enable("false")) multiplexer_4 (
    .in0(out_12), .in1(demultiplexer_4_out0), .out(multiplexer_4_out), .sel(not_1_out));
  D_Flip_Flop #(.trigger("falling")) d_ff_1 (
    .clk(clock_1_out), .D(multiplexer_1_out), .Q(out_6));  // open: Qn, preset, en, reset
  D_Flip_Flop #(.trigger("falling")) d_ff_2 (
    .clk(clock_1_out), .D(multiplexer_2_out), .Q(out_8));  // open: Qn, preset, en, reset
  D_Flip_Flop #(.trigger("falling")) d_ff_3 (
    .clk(clock_1_out), .D(multiplexer_3_out), .Q(out_10));  // open: Qn, preset, en, reset
  D_Flip_Flop #(.trigger("falling")) d_ff_4 (
    .clk(clock_1_out), .D(multiplexer_4_out), .Q(out_12));  // open: Qn, preset, en, reset
  Clock clock_1 (.out(clock_1_out));
  not not_2 (not_2_out, not_1_out);
  Multiplexer #(.enable("false")) multiplexer_5 (
    .in0(out_7), .in1(demultiplexer_1_out1), .out(multiplexer_5_out), .sel(not_2_out));
  Multiplexer #(.enable("false")) multiplexer_6 (
    .in0(out_9), .in1(demultiplexer_2_out1), .out(multiplexer_6_out), .sel(not_2_out));
  Multiplexer #(.enable("false")) multiplexer_7 (
    .in0(out_11), .in1(demultiplexer_3_out1), .out(multiplexer_7_out), .sel(not_2_out));
  Multiplexer #(.enable("false")) multiplexer_8 (
    .in0(out_13), .in1(demultiplexer_4_out1), .out(multiplexer_8_out), .sel(not_2_out));
  D_Flip_Flop #(.trigger("falling")) d_ff_5 (
    .clk(clock_1_out), .D(multiplexer_5_out), .Q(out_7));  // open: Qn, preset, en, reset
  D_Flip_Flop #(.trigger("falling")) d_ff_6 (
    .clk(clock_1_out), .D(multiplexer_6_out), .Q(out_9));  // open: Qn, preset, en, reset
  D_Flip_Flop #(.trigger("falling")) d_ff_7 (
    .clk(clock_1_out), .D(multiplexer_7_out), .Q(out_11));  // open: Qn, preset, en, reset
  D_Flip_Flop #(.trigger("falling")) d_ff_8 (
    .clk(clock_1_out), .D(multiplexer_8_out), .Q(out_13));  // open: Qn, preset, en, reset
endmodule
