// Logisim project SUMADOR.circ as structural Verilog: 1 circuit, main circuit main
module main (
  input  in_1,
  input  in_2,
  input  in_3,
  input  in_4,
  input  in_5,
  input  in_6,
  input  in_7,
  input  in_8,
  output out_9,
  output out_10,
  output out_11,
  output out_12,
  output out_13
);

  wire and_1_out, and_2_out, and_3_out, and_4_out, and_5_out, and_6_out, and_7_out, or_1_out, or_2_out,
       xor_2_out, xor_4_out, xor_6_out;

  and and_1 (and_1_out, in_4, in_8);
  xor xor_1 (out_13, in_4, in_8);
  xor xor_2 (xor_2_out, and_1_out, in_3);
  and and_2 (and_2_out, xor_2_out, in_7);
  and and_3 (and_3_out, and_1_out, in_3);
  xor xor_3 (out_12, xor_2_out, in_7);
  or or_1 (or_1_out, and_3_out, and_2_out);
  xor xor_4 (xor_4_out, in_2, or_1_out);
  and and_4 (and_4_out, xor_4_out, in_6);
  and and_5 (and_5_out, in_2, or_1_out);
  xor xor_5 (out_11, xor_4_out, in_6);
  or or_2 (or_2_out, and_5_out, and_4_out);
  xor xor_6 (xor_6_out, or_2_out, in_1);
  and and_6 (and_6_out, xor_6_out, in_5);
  and and_7 (and_7_out, or_2_out, in_1);
  xor xor_7 (out_10, xor_6_out, in_5);
  or or_3 (out_9, and_7_out, and_6_out);
endmodule
