// Logisim project Circuito v2.circ as structural Verilog: 1 circuit, main circuit main
module main (
  input  Bit_0,
  input  Bit_1,
  input  \Dirección ,
  input  \Operación ,
  output Salida_0,
  output Salida_1
);

  wire and_1_out, and_2_out, and_3_out, and_4_out, and_5_out, and_6_out, and_7_out, and_8_out, and_9_out,
       and_10_out, and_11_out, and_12_out, \Dirección_0_0_q , \Dirección_0_1_q , \Dirección_1_0_q ,
       \Dirección_1_1_q , not_1_out, not_2_out, not_3_out, not_4_out, not_5_out, or_1_out, or_2_out,
       Reloj_out;

  Clock Reloj (.out(Reloj_out));
  not not_1 (not_1_out, \Dirección );
  not not_2 (not_2_out, \Dirección );
  and and_1 (and_1_out, Bit_0, not_1_out);
  and and_2 (and_2_out, \Dirección , Bit_0);
  and and_3 (and_3_out, Bit_1, not_2_out);
  and and_4 (and_4_out, \Dirección , Bit_1);
  not not_3 (not_3_out, \Dirección );
  and and_5 (and_5_out, not_3_out, Reloj_out);
  D_Flip_Flop \Dirección_0_0  (.clk(and_5_out), .D(and_1_out), .Q(\Dirección_0_0_q ));  // open: Qn, preset, en, reset
  D_Flip_Flop \Dirección_0_1  (.clk(and_5_out), .D(and_3_out), .Q(\Dirección_0_1_q ));  // open: Qn, preset, en, reset
  and and_6 (and_6_out, \Dirección , Reloj_out);
  D_Flip_Flop \Dirección_1_0  (.clk(and_6_out), .D(and_2_out), .Q(\Dirección_1_0_q ));  // open: Qn, preset, en, reset
  D_Flip_Flop \Dirección_1_1  (.clk(and_6_out), .D(and_4_out), .Q(\Dirección_1_1_q ));  // open: Qn, preset, en, reset
  and and_7 (and_7_out, \Dirección_0_0_q , \Dirección_1_0_q );
  or or_1 (or_1_out, \Dirección_0_0_q , \Dirección_1_0_q );
  and and_8 (and_8_out, \Dirección_0_1_q , \Dirección_1_1_q );
  or or_2 (or_2_out, \Dirección_0_1_q , \Dirección_1_1_q );
  not not_4 (not_4_out, \Operación );
  not not_5 (not_5_out, \Operación );
  and and_9 (and_9_out, and_7_out, \Operación );
  or or_3 (Salida_0, and_9_out, and_10_out);
  and and_10 (and_10_out, or_1_out, not_4_out);
  and and_11 (and_11_out, and_8_out, \Operación );
  or or_4 (Salida_1, and_11_out, and_12_out);
  and and_12 (and_12_out, or_2_out, not_5_out);

  // Notes on the sheet:
  //   0 = OR
  //   1 = AND
endmodule
