// Logisim project Circuito.circ as structural Verilog: 1 circuit, main circuit main
module main (
  input  Bit,
  input  Bit_2,
  input  Memoria,
  input  OP,
  output out_5,
  output out_6,
  output out_7,
  output out_8,
  output out_9,
  output out_10
);

  wire and_1_out, and_2_out, and_3_out, and_4_out, and_5_out, and_6_out, and_7_out, and_8_out, and_9_out,
       and_10_out, and_11_out, and_12_out, and_13_out, and_14_out, clock_1_out, not_1_out, not_2_out,
       not_3_out, not_4_out, not_5_out, not_6_out, not_7_out, or_1_out, or_2_out, or_3_out, or_4_out,
       or_5_out, or_6_out;

  and and_1 (and_1_out, not_3_out, Bit_2);
  not not_1 (not_1_out, not_3_out);
  and and_2 (and_2_out, not_1_out, out_8);
  and and_3 (and_3_out, not_3_out, Bit);
  not not_2 (not_2_out, not_3_out);
  and and_4 (and_4_out, not_2_out, out_10);
  not not_3 (not_3_out, Memoria);
  or or_1 (or_1_out, and_1_out, and_2_out);
  or or_2 (or_2_out, and_3_out, and_4_out);
  Clock clock_1 (.out(clock_1_out));
  D_Flip_Flop #(.trigger("falling")) d_ff_1 (
    .clk(clock_1_out), .D(or_1_out), .Q(out_8));  // open: Qn, preset, en, reset
  D_Flip_Flop #(.trigger("falling")) d_ff_2 (
    .clk(clock_1_out), .D(or_2_out), .Q(out_10));  // open: Qn, preset, en, reset
  and and_5 (and_5_out, Memoria, Bit_2);
  not not_4 (not_4_out, Memoria);
  and and_6 (and_6_out, not_4_out, out_5);
  and and_7 (and_7_out, Memoria, Bit);
  not not_5 (not_5_out, Memoria);
  and and_8 (and_8_out, not_5_out, out_9);
  or or_3 (or_3_out, and_5_out, and_6_out);
  or or_4 (or_4_out, and_7_out, and_8_out);
  D_Flip_Flop #(.trigger("falling")) d_ff_3 (
    .clk(clock_1_out), .D(or_3_out), .Q(out_5));  // open: Qn, preset, en, reset
  D_Flip_Flop #(.trigger("falling")) d_ff_4 (
    .clk(clock_1_out), .D(or_4_out), .Q(out_9));  // open: Qn, preset, en, reset
  or or_5 (or_5_out, out_8, out_5);
  and and_9 (and_9_out, out_8, out_5);
  or or_6 (or_6_out, out_10, out_9);
  and and_10 (and_10_out, out_10, out_9);
  not not_6 (not_6_out, OP);
  and and_11 (and_11_out, not_6_out, or_5_out);
  and and_12 (and_12_out, OP, and_9_out);
  not not_7 (not_7_out, OP);
  and and_13 (and_13_out, not_7_out, or_6_out);
  and and_14 (and_14_out, OP, and_10_out);
  or or_7 (out_6, and_11_out, and_12_out);
  or or_8 (out_7, and_13_out, and_14_out);
endmodule
